# Fritzing sketch inventoneBuglarAlarmSystem (saved by Fritzing 0.9.3b)
breadboards: 1

parts:
  J1 = Piezo Speaker
  PIR1 = PIR sensor
  INVENTONE_1 = Invent One

nets:
  GND: J1.pin1, PIR1.GND, INVENTONE_1.GND
  N1: J1.pin2, INVENTONE_1.IO16
  VDD: PIR1.VDD, INVENTONE_1.5V
  N2: PIR1.SIG, INVENTONE_1.IO13

custom parts:
  Invent One: An IoT microcontroller based on the ESP8266 Wi-Fi chip.
