# Fritzing sketch inventoneButtonControlledLED (saved by Fritzing 0.9.3b)
breadboards: 1

parts:
  INVENTONE_1 = Invent One
  R1 = Resistor [tolerance=±5% resistance=220 package=THT]
  LED1 = LED - 5mm [color="Red (633nm)" package="5 mm [THT]"]
  S1 = Pushbutton [package="[THT]"]
  R2 = Resistor [tolerance=±5% resistance=10k package=THT]

nets:
  N1: INVENTONE_1.IO12, R1.Pin_1
  N2: INVENTONE_1.IO13, S1.Pin_3, S1.Pin_4, R2.Pin_1
  N3: INVENTONE_1.3V3, S1.Pin_1, S1.Pin_2
  N4: INVENTONE_1.GND, LED1.cathode, R2.Pin_0
  N5: R1.Pin_0, LED1.anode

custom parts:
  Invent One: An IoT microcontroller based on the ESP8266 Wi-Fi chip.
