# Fritzing sketch inventoneDistanceMeasuringSystem(LCD) (saved by Fritzing 0.9.1b)
breadboards: 1

parts:
  Part1 = SRF05 Ultrasonic Rangefinder
  Part2 = LCD1602-I2C
  Microcontoller_board1 = INVENT ONE V2

nets:
  VCC: Part1.VCC, Part2.VCC, Microcontoller_board1.5V
  N1: Part1.Trig, Microcontoller_board1.D5
  N2: Part1.Echo, Microcontoller_board1.D6
  GND: Part1.GND, Part2.GND, Microcontoller_board1.GND
  N3: Part2.SDA, Microcontoller_board1.D4
  N4: Part2.SCL, Microcontoller_board1.D3

custom parts:
  LCD1602-I2C: A standard character display, usually with 2x16 characters. Comes in many colors with LCM1602 IIC attached.
  INVENT ONE V2: An IoT (Internet of Things) development board built around the ESP8266 (ESP-12F) microcontoller/WiFi module. The aim of this device is to aid rapid prototyping of many engineering and technology projects, from blinky an LED to building a robot car and so on. The Invent One is geared towards different age groups, from kids to teenagers and to proffessional adults, it offers a gentle learning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
