# Fritzing sketch inventoneDistanceMeasuring_WebInterface (saved by Fritzing 0.9.3b)
breadboards: 1

parts:
  hc-sr1 = hc-sr04
  INVENTONE_1 = Invent One

nets:
  VCC: hc-sr1.VCC, INVENTONE_1.5V
  N1: hc-sr1.Trig, INVENTONE_1.IO13
  N2: hc-sr1.Echo, INVENTONE_1.IO12
  GND: hc-sr1.GND, INVENTONE_1.GND

custom parts:
  Invent One: An IoT microcontroller based on the ESP8266 Wi-Fi chip.
