# Fritzing sketch inventoneDotMatrix (saved by Fritzing 0.9.3b)

parts:
  INVENTONE_1 = Invent One
  Part1 = LED Matrix - Serial Interface - Red/Green/Blue

nets:
  5V: INVENTONE_1.5V, Part1.VCC
  N1: INVENTONE_1.IO16, Part1.SCK
  N2: INVENTONE_1.IO12, Part1.CS
  N3: INVENTONE_1.IO13, Part1.MOSI
  GND: INVENTONE_1.GND, Part1.GND

custom parts:
  Invent One: An IoT microcontroller based on the ESP8266 Wi-Fi chip.
