# Fritzing sketch inventoneLCD (saved by Fritzing 0.9.1b)
breadboards: 1

parts:
  Microcontoller_board1 = INVENT ONE V2
  Part1 = LCD1602-I2C

nets:
  5V: Microcontoller_board1.5V, Microcontoller_board1.D6, Microcontoller_board1.D5, Part1.VCC, Part1.SDA, Part1.SCL
  N1: Microcontoller_board1.RST, Microcontoller_board1.A4, Microcontoller_board1.D9, Microcontoller_board1.D8, Microcontoller_board1.D7
  N2: Microcontoller_board1.D4, Microcontoller_board1.D3, Microcontoller_board1.D2, Microcontoller_board1.D1, Microcontoller_board1.EN
  GND: Microcontoller_board1.GND, Part1.GND

custom parts:
  INVENT ONE V2: An IoT (Internet of Things) development board built around the ESP8266 (ESP-12F) microcontoller/WiFi module. The aim of this device is to aid rapid prototyping of many engineering and technology projects, from blinky an LED to building a robot car and so on. The Invent One is geared towards different age groups, from kids to teenagers and to proffessional adults, it offers a gentle learning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
  LCD1602-I2C: A standard character display, usually with 2x16 characters. Comes in many colors with LCM1602 IIC attached.
