# Fritzing sketch inventoneLedBrigthnessControl(Potentiometer) (saved by Fritzing 0.9.3b)
breadboards: 1

parts:
  R1 = Rotary Potentiometer (Small) [maximum_resistance=100kΩ package=THT]
  LED1 = LED - 5mm [color="Red (633nm)" package="5 mm [THT]"]
  INVENTONE_1 = Invent One
  R2 = Resistor [tolerance=±5% resistance=220 package=THT]

nets:
  N1: R1.leg1, INVENTONE_1.5V
  N2: R1.wiper, INVENTONE_1.IO5
  N3: R1.leg2, INVENTONE_1.GND, R2.Pin_1
  N4: LED1.cathode, INVENTONE_1.IO4
  N5: LED1.anode, R2.Pin_0

custom parts:
  Invent One: An IoT microcontroller based on the ESP8266 Wi-Fi chip.
