# Fritzing sketch inventoneLightBrightnessControl_WebInterface (saved by Fritzing 0.9.1b)

parts:
  Microcontoller_board1 = INVENT ONE V2
  LED1 = Ruby the Red LED

nets:
  N1: Microcontoller_board1.D4, LED1.anode
  N2: Microcontoller_board1.GND, LED1.cathode

custom parts:
  INVENT ONE V2: An IoT (Internet of Things) development board built around the ESP8266 (ESP-12F) microcontoller/WiFi module. The aim of this device is to aid rapid prototyping of many engineering and technology projects, from blinky an LED to building a robot car and so on. The Invent One is geared towards different age groups, from kids to teenagers and to proffessional adults, it offers a gentle learning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
