# Fritzing sketch inventoneSmartDoor (saved by Fritzing 0.9.3b)
breadboards: 1

parts:
  INVENTONE_1 = Invent One
  PIR1 = PIR sensor
  J1 = Basic Servo

nets:
  5V: INVENTONE_1.5V, PIR1.VDD, J1.vcc
  N1: INVENTONE_1.IO16, J1.pulse
  N2: INVENTONE_1.IO13, PIR1.SIG
  GND: INVENTONE_1.GND, PIR1.GND, J1.gnd

custom parts:
  Invent One: An IoT microcontroller based on the ESP8266 Wi-Fi chip.
