# Fritzing sketch inventoneSmartLightingSystem_LDR (saved by Fritzing 0.9.1b)
breadboards: 1

parts:
  R1 = Photocell (LDR) [package=THT]
  INVENTONE_1 = Invent One
  R2 = Resistor [tolerance=±5% resistance=10k package=THT]
  KY-1 = Keyes Relay [package=THT]
  LED1 = LEDs [package=led10mm]
  Part1 = Lilypad Battery Connect

nets:
  N1: R1.pin_0, INVENTONE_1.GND, R2.Pin_1, KY-1.ground
  N2: R1.pin_1, INVENTONE_1.ADC, R2.Pin_0
  N3: INVENTONE_1.IO13, KY-1.signal
  N4: INVENTONE_1.3V3, KY-1.power
  N5: KY-1.C, Part1.+
  N6: KY-1.NO, LED1.C
  N7: LED1.A, Part1.-

custom parts:
  Invent One: An IoT microcontroller based on the ESP8266 Wi-Fi chip.
  Keyes Relay: The Keyes 5V relay module is suitable for SCM development, home appliance control. It uses a 5V~12V TIL control signal which can control DC / AC signal.
  LEDs: LEDs Standard schematic elements and footprints for 5mm, 3mm, 1206, and 0603 sized LEDs. 5mm - Spark Fun Electronics SKU : COM-00529 (and others)
