# Fritzing sketch inventoneTemperature&HumidityMeasuringSystem (saved by Fritzing 0.9.1b)
breadboards: 1

parts:
  RHT1 = Humidity and Temperature Sensor RHT03
  Part1 = LCD1602-I2C
  R1 = Resistor [tolerance=±5% resistance=220 package="1206 [SMD]"]
  Microcontoller_board1 = INVENT ONE V2

nets:
  VCC: RHT1.Vcc, R1.Pin_0, Microcontoller_board1.5V
  N1: RHT1.Data-signal, R1.Pin_1, Microcontoller_board1.D7
  GND: RHT1.GND_2, Part1.GND, Microcontoller_board1.GND
  N2: Part1.SDA, Microcontoller_board1.D2
  N3: Part1.SCL, Microcontoller_board1.D4

custom parts:
  LCD1602-I2C: A standard character display, usually with 2x16 characters. Comes in many colors with LCM1602 IIC attached.
  INVENT ONE V2: An IoT (Internet of Things) development board built around the ESP8266 (ESP-12F) microcontoller/WiFi module. The aim of this device is to aid rapid prototyping of many engineering and technology projects, from blinky an LED to building a robot car and so on. The Invent One is geared towards different age groups, from kids to teenagers and to proffessional adults, it offers a gentle learning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
