# Fritzing sketch inventoneTemperatureMeasuringSystem_DS18B20 (saved by Fritzing 0.9.3b)
breadboards: 1

parts:
  INVENTONE_1 = Invent One
  DS1 = DS18B20 1-Wire Temperature Sensor [part_number=DS18B20]
  R1 = Resistor [tolerance=±5% resistance=47k package=THT]

nets:
  5V: INVENTONE_1.5V, DS1.VDD
  N1: INVENTONE_1.IO12, DS1.DQ, R1.Pin_0
  GND: INVENTONE_1.GND, DS1.GND

custom parts:
  Invent One: An IoT microcontroller based on the ESP8266 Wi-Fi chip.
