# Fritzing sketch inventoneTemperatureMeasuring_WebInterface (saved by Fritzing 0.9.1b)
breadboards: 1

parts:
  Microcontoller_board1 = INVENT ONE V2
  DHT1 = DHT22 Humidity and Temperature Sensor
  R1 = Resistor [tolerance=±5% resistance=220 package="0603 [SMD]"]

nets:
  N1: Microcontoller_board1.D8, R1.Pin_1
  N2: Microcontoller_board1.3V, DHT1.VDD
  GND: Microcontoller_board1.GND, DHT1.GND
  N3: DHT1.DATA, R1.Pin_0

custom parts:
  INVENT ONE V2: An IoT (Internet of Things) development board built around the ESP8266 (ESP-12F) microcontoller/WiFi module. The aim of this device is to aid rapid prototyping of many engineering and technology projects, from blinky an LED to building a robot car and so on. The Invent One is geared towards different age groups, from kids to teenagers and to proffessional adults, it offers a gentle learning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
