# Fritzing sketch inventoneWebControlledCar (saved by Fritzing 0.9.1b)

parts:
  S1 = H-Bridge with L298N
  M1 = DC Motor
  M2 = DC Motor
  VCC1 = Battery
  VCC2 = Battery
  VCC3 = Battery
  VCC4 = Battery
  Microcontoller_board1 = INVENT ONE V2

nets:
  N1: S1.12V, VCC1.+
  GND: S1.GND, VCC4.-, Microcontoller_board1.GND
  5V: S1.5V, Microcontoller_board1.5V
  N2: S1.ENA, S1.ENA-5V
  N3: S1.IN1, Microcontoller_board1.D6
  N4: S1.IN2, Microcontoller_board1.D5
  N5: S1.IN3, Microcontoller_board1.D8
  N6: S1.IN4, Microcontoller_board1.D7
  N7: S1.ENB, S1.ENB-5V
  N8: S1.M1-01, M2.pin_2
  N9: S1.M1-02, M2.pin_1
  N10: S1.M2-01, M1.pin_2
  N11: S1.M2-02, M1.pin_1
  N12: VCC1.-, VCC2.+
  N13: VCC2.-, VCC3.+
  N14: VCC3.-, VCC4.+

custom parts:
  H-Bridge with L298N: h-bridge
  INVENT ONE V2: An IoT (Internet of Things) development board built around the ESP8266 (ESP-12F) microcontoller/WiFi module. The aim of this device is to aid rapid prototyping of many engineering and technology projects, from blinky an LED to building a robot car and so on. The Invent One is geared towards different age groups, from kids to teenagers and to proffessional adults, it offers a gentle learning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
