# Fritzing sketch inventoneWebControlledLight (saved by Fritzing 0.9.1b)
breadboards: 1

parts:
  KY-1 = Keyes Relay [package=THT]
  LED1 = LEDs [package=led10mm]
  Part1 = Lilypad Battery Connect
  Microcontoller_board1 = INVENT ONE V2

nets:
  N1: KY-1.signal, Microcontoller_board1.D6
  N2: KY-1.power, Microcontoller_board1.5V
  N3: KY-1.ground, Microcontoller_board1.GND
  N4: KY-1.C, Part1.+
  N5: KY-1.NO, LED1.C
  N6: LED1.A, Part1.-

custom parts:
  Keyes Relay: The Keyes 5V relay module is suitable for SCM development, home appliance control. It uses a 5V~12V TIL control signal which can control DC / AC signal.
  LEDs: LEDs Standard schematic elements and footprints for 5mm, 3mm, 1206, and 0603 sized LEDs. 5mm - Spark Fun Electronics SKU : COM-00529 (and others)
  INVENT ONE V2: An IoT (Internet of Things) development board built around the ESP8266 (ESP-12F) microcontoller/WiFi module. The aim of this device is to aid rapid prototyping of many engineering and technology projects, from blinky an LED to building a robot car and so on. The Invent One is geared towards different age groups, from kids to teenagers and to proffessional adults, it offers a gentle learning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
